// Logisim project Register.circ as structural Verilog: 2 circuits, main circuit Register
module Register (
  input  [1:0] IN,
  input  Clock,
  output [1:0] Q
);

  FlipFlopDT flipflopdt_1 (.D(IN[0]), .Clock(Clock), .Q(Q[0]));  // open: nQ
  FlipFlopDT flipflopdt_2 (.D(IN[1]), .Clock(Clock), .Q(Q[1]));  // open: nQ
endmodule

module RegisterFile (
  input  [5:0] Register_write,
  input  [1:0] Write_content,
  input  [5:0] Register_read,
  output [1:0] Read_out
);

  wire and_1_out, and_2_out, and_3_out, and_4_out, and_5_out, and_6_out, and_7_out, and_8_out, and_9_out,
       and_10_out, and_11_out, and_12_out, and_13_out, and_14_out, and_15_out, and_16_out, and_17_out,
       and_18_out, and_19_out, and_20_out, and_21_out, and_22_out, and_23_out, and_24_out, and_25_out,
       and_26_out, and_27_out, and_28_out, and_29_out, and_30_out, and_31_out, and_32_out, and_33_out,
       and_34_out, and_35_out, and_36_out, and_37_out, and_38_out, and_39_out, and_40_out, and_41_out,
       and_42_out, and_43_out, and_44_out, and_45_out, and_46_out, and_47_out, and_48_out, and_49_out,
       and_50_out, and_51_out, and_52_out, and_53_out, and_54_out, and_55_out, and_56_out, and_57_out,
       and_58_out, and_59_out, and_60_out, and_61_out, and_62_out, and_63_out, and_64_out, clock_1_out,
       decoder_1_out_2, decoder_1_out_3, decoder_1_out_4, decoder_1_out_5, decoder_1_out_6, decoder_1_out_7,
       decoder_1_out_8, decoder_1_out_9, decoder_1_out_10, decoder_1_out_11, decoder_1_out_12,
       decoder_1_out_13, decoder_1_out_14, decoder_1_out_15, decoder_1_out_16, decoder_1_out_17,
       decoder_1_out_18, decoder_1_out_19, decoder_1_out_20, decoder_1_out_21, decoder_1_out_22,
       decoder_1_out_23, decoder_1_out_24, decoder_1_out_25, decoder_1_out_26, decoder_1_out_27,
       decoder_1_out_28, decoder_1_out_29, decoder_1_out_30, decoder_1_out_31, decoder_1_out_32,
       decoder_1_out_33, decoder_1_out_34, decoder_1_out_35, decoder_1_out_36, decoder_1_out_37,
       decoder_1_out_38, decoder_1_out_39, decoder_1_out_40, decoder_1_out_41, decoder_1_out_42,
       decoder_1_out_43, decoder_1_out_44, decoder_1_out_45, decoder_1_out_46, decoder_1_out_47,
       decoder_1_out_48, decoder_1_out_49, decoder_1_out_50, decoder_1_out_51, decoder_1_out_52,
       decoder_1_out_53, decoder_1_out_54, decoder_1_out_55, decoder_1_out_56, decoder_1_out_57,
       decoder_1_out_58, decoder_1_out_59, decoder_1_out_60, decoder_1_out_61, decoder_1_out_62,
       decoder_1_out_63, decoder_1_out_64, decoder_1_out_65;
  wire [1:0] register_1_q, register_2_q, register_3_q, register_4_q, register_5_q, register_6_q,
       register_7_q, register_8_q, register_9_q, register_10_q, register_11_q, register_12_q, register_13_q,
       register_14_q, register_15_q, register_16_q, register_17_q, register_18_q, register_19_q,
       register_20_q, register_21_q, register_22_q, register_23_q, register_24_q, register_25_q,
       register_26_q, register_27_q, register_28_q, register_29_q, register_30_q, register_31_q,
       register_32_q, register_33_q, register_34_q, register_35_q, register_36_q, register_37_q,
       register_38_q, register_39_q, register_40_q, register_41_q, register_42_q, register_43_q,
       register_44_q, register_45_q, register_46_q, register_47_q, register_48_q, register_49_q,
       register_50_q, register_51_q, register_52_q, register_53_q, register_54_q, register_55_q,
       register_56_q, register_57_q, register_58_q, register_59_q, register_60_q, register_61_q,
       register_62_q, register_63_q, register_64_q;

  Decoder decoder_1 (
    .in_1(Register_write), .out_2(decoder_1_out_2), .out_3(decoder_1_out_3), .out_4(decoder_1_out_4),
    .out_5(decoder_1_out_5), .out_6(decoder_1_out_6), .out_7(decoder_1_out_7), .out_8(decoder_1_out_8),
    .out_9(decoder_1_out_9), .out_10(decoder_1_out_10), .out_11(decoder_1_out_11), .out_12(decoder_1_out_12),
    .out_13(decoder_1_out_13), .out_14(decoder_1_out_14), .out_15(decoder_1_out_15),
    .out_16(decoder_1_out_16), .out_17(decoder_1_out_17), .out_18(decoder_1_out_18),
    .out_19(decoder_1_out_19), .out_20(decoder_1_out_20), .out_21(decoder_1_out_21),
    .out_22(decoder_1_out_22), .out_23(decoder_1_out_23), .out_24(decoder_1_out_24),
    .out_25(decoder_1_out_25), .out_26(decoder_1_out_26), .out_27(decoder_1_out_27),
    .out_28(decoder_1_out_28), .out_29(decoder_1_out_29), .out_30(decoder_1_out_30),
    .out_31(decoder_1_out_31), .out_32(decoder_1_out_32), .out_33(decoder_1_out_33),
    .out_34(decoder_1_out_34), .out_35(decoder_1_out_35), .out_36(decoder_1_out_36),
    .out_37(decoder_1_out_37), .out_38(decoder_1_out_38), .out_39(decoder_1_out_39),
    .out_40(decoder_1_out_40), .out_41(decoder_1_out_41), .out_42(decoder_1_out_42),
    .out_43(decoder_1_out_43), .out_44(decoder_1_out_44), .out_45(decoder_1_out_45),
    .out_46(decoder_1_out_46), .out_47(decoder_1_out_47), .out_48(decoder_1_out_48),
    .out_49(decoder_1_out_49), .out_50(decoder_1_out_50), .out_51(decoder_1_out_51),
    .out_52(decoder_1_out_52), .out_53(decoder_1_out_53), .out_54(decoder_1_out_54),
    .out_55(decoder_1_out_55), .out_56(decoder_1_out_56), .out_57(decoder_1_out_57),
    .out_58(decoder_1_out_58), .out_59(decoder_1_out_59), .out_60(decoder_1_out_60),
    .out_61(decoder_1_out_61), .out_62(decoder_1_out_62), .out_63(decoder_1_out_63),
    .out_64(decoder_1_out_64), .out_65(decoder_1_out_65));
  Clock clock_1 (.out(clock_1_out));
  and and_1 (and_1_out, decoder_1_out_65, clock_1_out);
  and and_2 (and_2_out, decoder_1_out_64, clock_1_out);
  and and_3 (and_3_out, decoder_1_out_63, clock_1_out);
  and and_4 (and_4_out, decoder_1_out_62, clock_1_out);
  and and_5 (and_5_out, decoder_1_out_61, clock_1_out);
  and and_6 (and_6_out, decoder_1_out_60, clock_1_out);
  and and_7 (and_7_out, decoder_1_out_59, clock_1_out);
  and and_8 (and_8_out, decoder_1_out_58, clock_1_out);
  and and_9 (and_9_out, decoder_1_out_57, clock_1_out);
  and and_10 (and_10_out, decoder_1_out_56, clock_1_out);
  and and_11 (and_11_out, decoder_1_out_55, clock_1_out);
  and and_12 (and_12_out, decoder_1_out_54, clock_1_out);
  and and_13 (and_13_out, decoder_1_out_53, clock_1_out);
  and and_14 (and_14_out, decoder_1_out_52, clock_1_out);
  and and_15 (and_15_out, decoder_1_out_51, clock_1_out);
  and and_16 (and_16_out, decoder_1_out_50, clock_1_out);
  and and_17 (and_17_out, decoder_1_out_49, clock_1_out);
  and and_18 (and_18_out, decoder_1_out_48, clock_1_out);
  and and_19 (and_19_out, decoder_1_out_47, clock_1_out);
  and and_20 (and_20_out, decoder_1_out_46, clock_1_out);
  and and_21 (and_21_out, decoder_1_out_45, clock_1_out);
  and and_22 (and_22_out, decoder_1_out_44, clock_1_out);
  and and_23 (and_23_out, decoder_1_out_43, clock_1_out);
  and and_24 (and_24_out, decoder_1_out_42, clock_1_out);
  and and_25 (and_25_out, decoder_1_out_41, clock_1_out);
  and and_26 (and_26_out, decoder_1_out_40, clock_1_out);
  and and_27 (and_27_out, decoder_1_out_39, clock_1_out);
  and and_28 (and_28_out, decoder_1_out_38, clock_1_out);
  and and_29 (and_29_out, decoder_1_out_37, clock_1_out);
  and and_30 (and_30_out, decoder_1_out_36, clock_1_out);
  and and_31 (and_31_out, decoder_1_out_35, clock_1_out);
  and and_32 (and_32_out, decoder_1_out_34, clock_1_out);
  and and_33 (and_33_out, decoder_1_out_33, clock_1_out);
  and and_34 (and_34_out, decoder_1_out_32, clock_1_out);
  and and_35 (and_35_out, decoder_1_out_31, clock_1_out);
  and and_36 (and_36_out, decoder_1_out_30, clock_1_out);
  and and_37 (and_37_out, decoder_1_out_29, clock_1_out);
  and and_38 (and_38_out, decoder_1_out_28, clock_1_out);
  and and_39 (and_39_out, decoder_1_out_27, clock_1_out);
  and and_40 (and_40_out, decoder_1_out_26, clock_1_out);
  and and_41 (and_41_out, decoder_1_out_25, clock_1_out);
  and and_42 (and_42_out, decoder_1_out_24, clock_1_out);
  and and_43 (and_43_out, decoder_1_out_23, clock_1_out);
  and and_44 (and_44_out, decoder_1_out_22, clock_1_out);
  and and_45 (and_45_out, decoder_1_out_21, clock_1_out);
  and and_46 (and_46_out, decoder_1_out_20, clock_1_out);
  and and_47 (and_47_out, decoder_1_out_19, clock_1_out);
  and and_48 (and_48_out, decoder_1_out_18, clock_1_out);
  and and_49 (and_49_out, decoder_1_out_17, clock_1_out);
  and and_50 (and_50_out, decoder_1_out_16, clock_1_out);
  and and_51 (and_51_out, decoder_1_out_15, clock_1_out);
  and and_52 (and_52_out, decoder_1_out_14, clock_1_out);
  and and_53 (and_53_out, decoder_1_out_13, clock_1_out);
  and and_54 (and_54_out, decoder_1_out_12, clock_1_out);
  and and_55 (and_55_out, decoder_1_out_11, clock_1_out);
  and and_56 (and_56_out, decoder_1_out_10, clock_1_out);
  and and_57 (and_57_out, decoder_1_out_9, clock_1_out);
  and and_58 (and_58_out, decoder_1_out_8, clock_1_out);
  and and_59 (and_59_out, decoder_1_out_7, clock_1_out);
  and and_60 (and_60_out, decoder_1_out_6, clock_1_out);
  and and_61 (and_61_out, decoder_1_out_5, clock_1_out);
  and and_62 (and_62_out, decoder_1_out_4, clock_1_out);
  and and_63 (and_63_out, decoder_1_out_3, clock_1_out);
  and and_64 (and_64_out, decoder_1_out_2, clock_1_out);
  Register register_1 (.IN(Write_content), .Clock(and_1_out), .Q(register_1_q));
  Register register_2 (.IN(Write_content), .Clock(and_2_out), .Q(register_2_q));
  Register register_3 (.IN(Write_content), .Clock(and_3_out), .Q(register_3_q));
  Register register_4 (.IN(Write_content), .Clock(and_4_out), .Q(register_4_q));
  Register register_5 (.IN(Write_content), .Clock(and_5_out), .Q(register_5_q));
  Register register_6 (.IN(Write_content), .Clock(and_6_out), .Q(register_6_q));
  Register register_7 (.IN(Write_content), .Clock(and_7_out), .Q(register_7_q));
  Register register_8 (.IN(Write_content), .Clock(and_8_out), .Q(register_8_q));
  Register register_9 (.IN(Write_content), .Clock(and_9_out), .Q(register_9_q));
  Register register_10 (.IN(Write_content), .Clock(and_10_out), .Q(register_10_q));
  Register register_11 (.IN(Write_content), .Clock(and_11_out), .Q(register_11_q));
  Register register_12 (.IN(Write_content), .Clock(and_12_out), .Q(register_12_q));
  Register register_13 (.IN(Write_content), .Clock(and_13_out), .Q(register_13_q));
  Register register_14 (.IN(Write_content), .Clock(and_14_out), .Q(register_14_q));
  Register register_15 (.IN(Write_content), .Clock(and_15_out), .Q(register_15_q));
  Register register_16 (.IN(Write_content), .Clock(and_16_out), .Q(register_16_q));
  Register register_17 (.IN(Write_content), .Clock(and_17_out), .Q(register_17_q));
  Register register_18 (.IN(Write_content), .Clock(and_18_out), .Q(register_18_q));
  Register register_19 (.IN(Write_content), .Clock(and_19_out), .Q(register_19_q));
  Register register_20 (.IN(Write_content), .Clock(and_20_out), .Q(register_20_q));
  Register register_21 (.IN(Write_content), .Clock(and_21_out), .Q(register_21_q));
  Register register_22 (.IN(Write_content), .Clock(and_22_out), .Q(register_22_q));
  Register register_23 (.IN(Write_content), .Clock(and_23_out), .Q(register_23_q));
  Register register_24 (.IN(Write_content), .Clock(and_24_out), .Q(register_24_q));
  Register register_25 (.IN(Write_content), .Clock(and_25_out), .Q(register_25_q));
  Register register_26 (.IN(Write_content), .Clock(and_26_out), .Q(register_26_q));
  Register register_27 (.IN(Write_content), .Clock(and_27_out), .Q(register_27_q));
  Register register_28 (.IN(Write_content), .Clock(and_28_out), .Q(register_28_q));
  Register register_29 (.IN(Write_content), .Clock(and_29_out), .Q(register_29_q));
  Register register_30 (.IN(Write_content), .Clock(and_30_out), .Q(register_30_q));
  Register register_31 (.IN(Write_content), .Clock(and_31_out), .Q(register_31_q));
  Register register_32 (.IN(Write_content), .Clock(and_32_out), .Q(register_32_q));
  Register register_33 (.IN(Write_content), .Clock(and_33_out), .Q(register_33_q));
  Register register_34 (.IN(Write_content), .Clock(and_34_out), .Q(register_34_q));
  Register register_35 (.IN(Write_content), .Clock(and_35_out), .Q(register_35_q));
  Register register_36 (.IN(Write_content), .Clock(and_36_out), .Q(register_36_q));
  Register register_37 (.IN(Write_content), .Clock(and_37_out), .Q(register_37_q));
  Register register_38 (.IN(Write_content), .Clock(and_38_out), .Q(register_38_q));
  Register register_39 (.IN(Write_content), .Clock(and_39_out), .Q(register_39_q));
  Register register_40 (.IN(Write_content), .Clock(and_40_out), .Q(register_40_q));
  Register register_41 (.IN(Write_content), .Clock(and_41_out), .Q(register_41_q));
  Register register_42 (.IN(Write_content), .Clock(and_42_out), .Q(register_42_q));
  Register register_43 (.IN(Write_content), .Clock(and_43_out), .Q(register_43_q));
  Register register_44 (.IN(Write_content), .Clock(and_44_out), .Q(register_44_q));
  Register register_45 (.IN(Write_content), .Clock(and_45_out), .Q(register_45_q));
  Register register_46 (.IN(Write_content), .Clock(and_46_out), .Q(register_46_q));
  Register register_47 (.IN(Write_content), .Clock(and_47_out), .Q(register_47_q));
  Register register_48 (.IN(Write_content), .Clock(and_48_out), .Q(register_48_q));
  Register register_49 (.IN(Write_content), .Clock(and_49_out), .Q(register_49_q));
  Register register_50 (.IN(Write_content), .Clock(and_50_out), .Q(register_50_q));
  Register register_51 (.IN(Write_content), .Clock(and_51_out), .Q(register_51_q));
  Register register_52 (.IN(Write_content), .Clock(and_52_out), .Q(register_52_q));
  Register register_53 (.IN(Write_content), .Clock(and_53_out), .Q(register_53_q));
  Register register_54 (.IN(Write_content), .Clock(and_54_out), .Q(register_54_q));
  Register register_55 (.IN(Write_content), .Clock(and_55_out), .Q(register_55_q));
  Register register_56 (.IN(Write_content), .Clock(and_56_out), .Q(register_56_q));
  Register register_57 (.IN(Write_content), .Clock(and_57_out), .Q(register_57_q));
  Register register_58 (.IN(Write_content), .Clock(and_58_out), .Q(register_58_q));
  Register register_59 (.IN(Write_content), .Clock(and_59_out), .Q(register_59_q));
  Register register_60 (.IN(Write_content), .Clock(and_60_out), .Q(register_60_q));
  Register register_61 (.IN(Write_content), .Clock(and_61_out), .Q(register_61_q));
  Register register_62 (.IN(Write_content), .Clock(and_62_out), .Q(register_62_q));
  Register register_63 (.IN(Write_content), .Clock(and_63_out), .Q(register_63_q));
  Register register_64 (.IN(Write_content), .Clock(and_64_out), .Q(register_64_q));
  Multiplexer_64 multiplexer_64_1 (
    .out_66(Read_out), .in_1(register_64_q), .in_2(register_63_q), .in_3(register_62_q),
    .in_4(register_61_q), .in_5(register_60_q), .in_6(register_59_q), .in_7(register_58_q),
    .in_8(register_57_q), .in_9(register_56_q), .in_10(register_55_q), .in_11(register_54_q),
    .in_12(register_53_q), .in_13(register_52_q), .in_14(register_51_q), .in_15(register_50_q),
    .in_16(register_49_q), .in_17(register_48_q), .in_18(register_47_q), .in_19(register_46_q),
    .in_20(register_45_q), .in_21(register_44_q), .in_22(register_43_q), .in_23(register_42_q),
    .in_24(register_41_q), .in_25(register_40_q), .in_26(register_39_q), .in_27(register_38_q),
    .in_28(register_37_q), .in_29(register_36_q), .in_30(register_35_q), .in_31(register_34_q),
    .in_32(register_33_q), .in_33(register_32_q), .in_34(register_31_q), .in_35(register_30_q),
    .in_36(register_29_q), .in_37(register_28_q), .in_38(register_27_q), .in_39(register_26_q),
    .in_40(register_25_q), .in_41(register_24_q), .in_42(register_23_q), .in_43(register_22_q),
    .in_44(register_21_q), .in_45(register_20_q), .in_46(register_19_q), .in_47(register_18_q),
    .in_48(register_17_q), .in_49(register_16_q), .in_50(register_15_q), .in_51(register_14_q),
    .in_52(register_13_q), .in_53(register_12_q), .in_54(register_11_q), .in_55(register_10_q),
    .in_56(register_9_q), .in_57(register_8_q), .in_58(register_7_q), .in_59(register_6_q),
    .in_60(register_5_q), .in_61(register_4_q), .in_62(register_3_q), .in_63(register_2_q),
    .in_64(register_1_q), .Select(Register_read));

  // Notes on the sheet:
  //   Clock
endmodule
