// Logisim project Selector.circ as structural Verilog: 2 circuits, main circuit Multiplexer 64
module Multiplexer_64 (
  input  [1:0] in_1,
  input  [1:0] in_2,
  input  [1:0] in_3,
  input  [1:0] in_4,
  input  [1:0] in_5,
  input  [1:0] in_6,
  input  [1:0] in_7,
  input  [1:0] in_8,
  input  [1:0] in_9,
  input  [1:0] in_10,
  input  [1:0] in_11,
  input  [1:0] in_12,
  input  [1:0] in_13,
  input  [1:0] in_14,
  input  [1:0] in_15,
  input  [1:0] in_16,
  input  [1:0] in_17,
  input  [1:0] in_18,
  input  [1:0] in_19,
  input  [1:0] in_20,
  input  [1:0] in_21,
  input  [1:0] in_22,
  input  [1:0] in_23,
  input  [1:0] in_24,
  input  [1:0] in_25,
  input  [1:0] in_26,
  input  [1:0] in_27,
  input  [1:0] in_28,
  input  [1:0] in_29,
  input  [1:0] in_30,
  input  [1:0] in_31,
  input  [1:0] in_32,
  output [1:0] out_33
);

  wire [1:0] or_1_out, or_2_out, undriven;

  assign or_1_out = in_1 | undriven | in_2 | undriven | in_3 | undriven | in_4 | undriven | in_5 | undriven | in_6 | undriven | in_7 | undriven | in_8 | undriven | in_9 | undriven | in_10 | undriven | in_11 | undriven | in_12 | undriven | in_13 | undriven | in_14 | undriven | in_15 | undriven | in_16;  // OR_Gate or_1, 2 bits wide
  assign or_2_out = in_17 | undriven | in_18 | in_19 | in_20 | in_21 | in_22 | in_23 | in_24 | in_25 | in_26 | in_27 | in_28 | in_29 | in_30 | in_31 | in_32;  // OR_Gate or_2, 2 bits wide
  assign out_33 = or_1_out | or_2_out;  // OR_Gate or_3, 2 bits wide
endmodule

module Decoder (
  input  in_1,
  input  in_2,
  input  in_3,
  input  in_4,
  input  in_5,
  input  in_6,
  output out_7,
  output out_8,
  output out_9,
  output out_10,
  output out_11,
  output out_12,
  output out_13,
  output out_14,
  output out_15,
  output out_16,
  output out_17,
  output out_18,
  output out_19,
  output out_20,
  output out_21,
  output out_22,
  output out_23,
  output out_24,
  output out_25,
  output out_26,
  output out_27,
  output out_28,
  output out_29,
  output out_30,
  output out_31,
  output out_32,
  output out_33,
  output out_34,
  output out_35,
  output out_36,
  output out_37,
  output out_38,
  output out_39,
  output out_40,
  output out_41,
  output out_42,
  output out_43,
  output out_44,
  output out_45,
  output out_46,
  output out_47,
  output out_48,
  output out_49,
  output out_50,
  output out_51,
  output out_52,
  output out_53,
  output out_54,
  output out_55,
  output out_56,
  output out_57,
  output out_58,
  output out_59,
  output out_60,
  output out_61,
  output out_62,
  output out_63,
  output out_64,
  output out_65,
  output out_66,
  output out_67,
  output out_68,
  output out_69,
  output out_70
);

  and and_1 (out_7, ~in_1, ~in_2, ~in_3, ~in_4, ~in_5, ~in_6);  // AND_Gate
  and and_2 (out_8, ~in_1, ~in_2, ~in_3, ~in_4, ~in_5, in_6);  // AND_Gate
  and and_3 (out_9, ~in_1, ~in_2, ~in_3, ~in_4, in_5, ~in_6);  // AND_Gate
  and and_4 (out_10, ~in_1, ~in_2, ~in_3, ~in_4, in_5, in_6);  // AND_Gate
  and and_5 (out_11, ~in_1, ~in_2, ~in_3, in_4, ~in_5, ~in_6);  // AND_Gate
  and and_6 (out_12, ~in_1, ~in_2, ~in_3, in_4, ~in_5, in_6);  // AND_Gate
  and and_7 (out_13, ~in_1, ~in_2, ~in_3, in_4, in_5, ~in_6);  // AND_Gate
  and and_8 (out_14, ~in_1, ~in_2, ~in_3, in_4, in_5, in_6);  // AND_Gate
  and and_9 (out_15, ~in_1, ~in_2, in_3, ~in_4, ~in_5, ~in_6);  // AND_Gate
  and and_10 (out_16, ~in_1, ~in_2, in_3, ~in_4, ~in_5, in_6);  // AND_Gate
  and and_11 (out_17, ~in_1, ~in_2, in_3, ~in_4, in_5, ~in_6);  // AND_Gate
  and and_12 (out_18, ~in_1, ~in_2, in_3, ~in_4, in_5, in_6);  // AND_Gate
  and and_13 (out_19, ~in_1, ~in_2, in_3, in_4, ~in_5, ~in_6);  // AND_Gate
  and and_14 (out_20, ~in_1, ~in_2, in_3, in_4, ~in_5, in_6);  // AND_Gate
  and and_15 (out_21, ~in_1, ~in_2, in_3, in_4, in_5, ~in_6);  // AND_Gate
  and and_16 (out_22, ~in_1, ~in_2, in_3, in_4, in_5, in_6);  // AND_Gate
  and and_17 (out_23, ~in_1, in_2, in_3, ~in_4, ~in_5, ~in_6);  // AND_Gate
  and and_18 (out_24, ~in_1, in_2, in_3, ~in_4, ~in_5, in_6);  // AND_Gate
  and and_19 (out_25, ~in_1, in_2, in_3, ~in_4, in_5, ~in_6);  // AND_Gate
  and and_20 (out_26, ~in_1, in_2, in_3, ~in_4, in_5, in_6);  // AND_Gate
  and and_21 (out_27, ~in_1, in_2, in_3, in_4, ~in_5, ~in_6);  // AND_Gate
  and and_22 (out_28, ~in_1, in_2, in_3, in_4, ~in_5, in_6);  // AND_Gate
  and and_23 (out_29, ~in_1, in_2, in_3, in_4, in_5, ~in_6);  // AND_Gate
  and and_24 (out_30, ~in_1, in_2, in_3, in_4, in_5, in_6);  // AND_Gate
  and and_25 (out_31, in_1, in_2, in_3, ~in_4, ~in_5, ~in_6);  // AND_Gate
  and and_26 (out_32, in_1, in_2, in_3, ~in_4, ~in_5, in_6);  // AND_Gate
  and and_27 (out_33, in_1, in_2, in_3, ~in_4, in_5, ~in_6);  // AND_Gate
  and and_28 (out_34, in_1, in_2, in_3, ~in_4, in_5, in_6);  // AND_Gate
  and and_29 (out_35, in_1, in_2, in_3, in_4, ~in_5, ~in_6);  // AND_Gate
  and and_30 (out_36, in_1, in_2, in_3, in_4, ~in_5, in_6);  // AND_Gate
  and and_31 (out_37, in_1, in_2, in_3, in_4, in_5, ~in_6);  // AND_Gate
  and and_32 (out_38, in_1, in_2, in_3, in_4, in_5, in_6);
  and and_33 (out_39, in_1, ~in_2, ~in_3, ~in_4, ~in_5, ~in_6);  // AND_Gate
  and and_34 (out_40, in_1, ~in_2, ~in_3, ~in_4, ~in_5, in_6);  // AND_Gate
  and and_35 (out_41, in_1, ~in_2, ~in_3, ~in_4, in_5, ~in_6);  // AND_Gate
  and and_36 (out_42, in_1, ~in_2, ~in_3, ~in_4, in_5, in_6);  // AND_Gate
  and and_37 (out_43, in_1, ~in_2, ~in_3, in_4, ~in_5, ~in_6);  // AND_Gate
  and and_38 (out_44, in_1, ~in_2, ~in_3, in_4, ~in_5, in_6);  // AND_Gate
  and and_39 (out_45, in_1, ~in_2, ~in_3, in_4, in_5, ~in_6);  // AND_Gate
  and and_40 (out_46, in_1, ~in_2, ~in_3, in_4, in_5, in_6);  // AND_Gate
  and and_41 (out_47, in_1, ~in_2, in_3, ~in_4, ~in_5, ~in_6);  // AND_Gate
  and and_42 (out_48, in_1, ~in_2, in_3, ~in_4, ~in_5, in_6);  // AND_Gate
  and and_43 (out_49, in_1, ~in_2, in_3, ~in_4, in_5, ~in_6);  // AND_Gate
  and and_44 (out_50, in_1, ~in_2, in_3, ~in_4, in_5, in_6);  // AND_Gate
  and and_45 (out_51, in_1, ~in_2, in_3, in_4, ~in_5, ~in_6);  // AND_Gate
  and and_46 (out_52, in_1, ~in_2, in_3, in_4, ~in_5, in_6);  // AND_Gate
  and and_47 (out_53, in_1, ~in_2, in_3, in_4, in_5, ~in_6);  // AND_Gate
  and and_48 (out_54, in_1, ~in_2, in_3, in_4, in_5, in_6);  // AND_Gate
  and and_49 (out_55, in_1, in_2, ~in_3, ~in_4, ~in_5, ~in_6);  // AND_Gate
  and and_50 (out_56, in_1, in_2, ~in_3, ~in_4, ~in_5, in_6);  // AND_Gate
  and and_51 (out_57, in_1, in_2, ~in_3, ~in_4, in_5, ~in_6);  // AND_Gate
  and and_52 (out_58, in_1, in_2, ~in_3, ~in_4, in_5, in_6);  // AND_Gate
  and and_53 (out_59, in_1, in_2, ~in_3, in_4, ~in_5, ~in_6);  // AND_Gate
  and and_54 (out_60, in_1, in_2, ~in_3, in_4, ~in_5, in_6);  // AND_Gate
  and and_55 (out_61, in_1, in_2, ~in_3, in_4, in_5, ~in_6);  // AND_Gate
  and and_56 (out_62, in_1, in_2, ~in_3, in_4, in_5, in_6);  // AND_Gate
  and and_57 (out_63, in_1, in_2, in_3, ~in_4, ~in_5, ~in_6);  // AND_Gate
  and and_58 (out_64, in_1, in_2, in_3, ~in_4, ~in_5, in_6);  // AND_Gate
  and and_59 (out_65, in_1, in_2, in_3, ~in_4, in_5, ~in_6);  // AND_Gate
  and and_60 (out_66, in_1, in_2, in_3, ~in_4, in_5, in_6);  // AND_Gate
  and and_61 (out_67, in_1, in_2, in_3, in_4, ~in_5, ~in_6);  // AND_Gate
  and and_62 (out_68, in_1, in_2, in_3, in_4, ~in_5, in_6);  // AND_Gate
  and and_63 (out_69, in_1, in_2, in_3, in_4, in_5, ~in_6);  // AND_Gate
  and and_64 (out_70, in_1, in_2, in_3, in_4, in_5, in_6);
endmodule
